// Logisim project pres.circ as structural Verilog: 15 circuits, main circuit 2.D flip flop
module _1_Logic_Gates (
  input  in_1,
  input  in_2,
  input  in_3,
  input  in_4,
  input  in_5,
  input  in_6,
  input  in_7,
  input  [2:0] in_8,
  input  [3:0] _4_bit_wire,
  input  [2:0] Multi_Bit_AND,
  input  [2:0] in_11,
  output out_12,
  output out_13,
  output out_14,
  output out_15,
  output [2:0] out_16,
  output out_17,
  output [2:0] out_18,
  output out_19,
  output out_20,
  output out_21,
  output out_22,
  output [2:0] out_23
);

  and and_1 (out_12, in_1, in_2);
  not not_1 (out_13, in_3);
  or or_1 (out_14, in_4, in_5);
  nand nand_1 (out_15, in_6, in_7);
  assign out_23 = Multi_Bit_AND & in_11;  // AND_Gate and_2, 3 bits wide

  assign out_16 = in_8;
  assign out_17 = _4_bit_wire[0];
  assign out_18 = _4_bit_wire[3:1];
  assign out_19 = _4_bit_wire[0];
  assign out_20 = _4_bit_wire[1];
  assign out_21 = _4_bit_wire[2];
  assign out_22 = _4_bit_wire[3];

  // Notes on the sheet:
  //   Input pin (square)
  //   AND
  //   NOT
  //   OR
  //   NAND
  //   Splitter
  //   Multi-Bit wire
  //   Output pin (round)
endmodule

module _2_D_flip_flop (
  input  Data,
  input  GateKeeper,
  input  Data_2,
  input  Gatekeeper_2,
  input  in_5,
  input  Data_3,
  output Q,
  output out_8,
  output Q_2
);

  wire nand_1_out, nand_2_out, nand_3_out, nand_4_out, nand_5_out, nand_6_out, nand_8_out, nand_9_out,
       nand_10_out, nand_12_out, not_1_out, not_2_out, not_3_out;

  not not_1 (not_1_out, Data);
  not not_2 (not_2_out, Gatekeeper_2);
  nand nand_1 (nand_1_out, Data, GateKeeper);
  nand nand_2 (nand_2_out, not_1_out, GateKeeper);
  nand nand_3 (nand_3_out, Data_2, not_2_out);
  nand nand_4 (nand_4_out, nand_3_out, not_2_out);
  not not_3 (not_3_out, not_2_out);
  nand nand_5 (nand_5_out, nand_3_out, nand_6_out);
  nand nand_6 (nand_6_out, nand_5_out, nand_4_out);
  nand nand_7 (Q, nand_1_out, nand_8_out);
  nand nand_8 (nand_8_out, Q, nand_2_out);
  D_Flip_Flop d_ff_1 (.clk(in_5), .D(Data_3), .Q(Q_2), .en(1'b1));  // open: Qn, preset, reset
  nand nand_9 (nand_9_out, nand_5_out, not_3_out);
  nand nand_10 (nand_10_out, nand_9_out, not_3_out);
  nand nand_11 (out_8, nand_9_out, nand_12_out);
  nand nand_12 (nand_12_out, out_8, nand_10_out);

  // Notes on the sheet:
  //   1:pass through
  //   0:remember value
  //   Remembers on the rising edge
  //   We can remember one bit.
  //   Triangle = Gatekeeper / Clock
  //   There's also an enable.
  //   Flipflop ignores everything if 0
  //   Master-Slave D flip-flop
endmodule

module _3_Register (
  input  Clock,
  input  in_2,
  input  in_3,
  input  in_4,
  input  in_5,
  input  in_6,
  input  in_7,
  input  in_8,
  input  in_9,
  output out_10,
  output out_11,
  output out_12,
  output out_13,
  output out_14,
  output out_15,
  output out_16,
  output out_17
);

  wire button_1_out;

  Button button_1 (.out(button_1_out));
  D_Flip_Flop d_ff_1 (.clk(Clock), .D(in_2), .Q(out_10));  // open: Qn, preset, en, reset
  D_Flip_Flop d_ff_2 (.clk(Clock), .D(in_3), .Q(out_11));  // open: Qn, preset, en, reset
  D_Flip_Flop d_ff_3 (.clk(Clock), .D(in_4), .Q(out_12));  // open: Qn, preset, en, reset
  D_Flip_Flop d_ff_4 (.clk(Clock), .D(in_5), .Q(out_13));  // open: Qn, preset, en, reset
  Register #(.width(4)) register_1 (
    .D({in_9, in_8, in_7, in_6}), .Q({out_17, out_16, out_15, out_14}), .clk(button_1_out));  // open: en, clr
endmodule

module _4__Multiplexer (
  input  _0,
  input  _1,
  input  Selector,
  input  in_4,
  input  in_5,
  input  in_6,
  input  in_7,
  input  in_8,
  input  in_9,
  output out_10,
  output out_11,
  output out_12
);

  wire and_1_out, and_2_out, multiplexer_2_out, multiplexer_3_out, not_1_out;

  not not_1 (not_1_out, Selector);
  Multiplexer #(.enable("false")) multiplexer_1 (.in0(_0), .in1(_1), .out(out_11), .sel(Selector));
  and and_1 (and_1_out, _0, not_1_out);
  and and_2 (and_2_out, _1, Selector);
  Multiplexer #(.enable("false")) multiplexer_2 (.in0(in_6), .in1(in_7), .out(multiplexer_2_out), .sel(in_4));
  Multiplexer #(.enable("false")) multiplexer_3 (.in0(in_8), .in1(in_9), .out(multiplexer_3_out), .sel(in_4));
  or or_1 (out_10, and_1_out, and_2_out);
  Multiplexer #(.enable("false")) multiplexer_4 (
    .in0(multiplexer_2_out), .in1(multiplexer_3_out), .out(out_12), .sel(in_5));
  Multiplexer #(.select(2), .enable("false")) multiplexer_5 ();  // open: in0, in1, in2, in3, out, sel

  // Notes on the sheet:
  //   Multiplexers: Choose which input is output
  //   Inputs
  //   4-input mux made out of 2-input muxs
endmodule

module _5__ALU (
  input  [7:0] Arguments,
  input  [1:0] in_2,
  input  [7:0] _0__Addition,
  output [7:0] Output
);

  wire [7:0] adder_1_out, negator_1_out, subtractor_1_out;

  Adder adder_1 (.a(Arguments), .b(_0__Addition), .out(adder_1_out));  // open: cin, cout
  Subtractor subtractor_1 (.a(Arguments), .b(_0__Addition), .out(subtractor_1_out));  // open: bin, bout
  Negator negator_1 (.in(Arguments), .out(negator_1_out));
  Multiplexer #(.select(2), .width(8), .enable("false")) multiplexer_1 (
    .in0(adder_1_out), .in1(subtractor_1_out), .in2(negator_1_out), .in3(Arguments), .out(Output), .sel(in_2));

  // Notes on the sheet:
  //   2: Negation
  //   3: Pass through
  //   Arithmetic logic unit
  //   1: Subtraction
  //   What if inputs to a mux were mathimatical functions?
  //   Function selector
  //   Look at its modular appearance
endmodule

module _6__Decoder (
  input  in_1,
  input  in_2,
  output _0,
  output _1,
  output _2,
  output _3,
  output out_7,
  output out_8,
  output out_9,
  output out_10
);

  wire not_1_out, not_2_out, not_3_out, not_4_out;

  not not_1 (not_1_out, in_1);
  not not_2 (not_2_out, in_2);
  not not_3 (not_3_out, in_1);
  not not_4 (not_4_out, in_2);
  Decoder #(.select(2), .enable("false")) decoder_1 (
    .out0(out_7), .out1(out_8), .out2(out_9), .out3(out_10), .sel({in_1, in_2}));
  and and_1 (_0, not_1_out, not_2_out);
  and and_2 (_1, not_3_out, in_2);
  and and_3 (_2, in_1, not_4_out);
  and and_4 (_3, in_1, in_2);

  // Notes on the sheet:
  //   Decoder: Turn on the wire corresponding to the input number
endmodule

module _7__CPU_A (
  input  [1:0] in_1,
  input  [7:0] in_2,
  input  [1:0] Reg_A,
  input  [1:0] Reg_B,
  input  [1:0] Which_function,
  output [7:0] out_6
);

  wire button_1_out, decoder_1_out0, decoder_1_out1, decoder_1_out2, decoder_1_out3;
  wire [7:0] multiplexer_1_out, multiplexer_2_out, register_1_q, register_2_q, register_3_q, register_4_q;

  Decoder #(.select(2), .enable("false")) decoder_1 (
    .out0(decoder_1_out0), .out1(decoder_1_out1), .out2(decoder_1_out2), .out3(decoder_1_out3), .sel(in_1));
  Button button_1 (.out(button_1_out));
  Register register_1 (.D(in_2), .en(decoder_1_out0), .Q(register_1_q), .clk(button_1_out));  // open: clr
  Register register_2 (.D(in_2), .en(decoder_1_out1), .Q(register_2_q), .clk(button_1_out));  // open: clr
  Register register_3 (.D(in_2), .en(decoder_1_out2), .Q(register_3_q), .clk(button_1_out));  // open: clr
  Register register_4 (.D(in_2), .en(decoder_1_out3), .Q(register_4_q), .clk(button_1_out));  // open: clr
  Multiplexer #(.select(2), .width(8), .enable("false")) multiplexer_1 (
    .in0(register_1_q), .in1(register_2_q), .in2(register_3_q), .in3(register_4_q), .out(multiplexer_1_out),
    .sel(Reg_A));
  Multiplexer #(.select(2), .width(8), .enable("false")) multiplexer_2 (
    .in0(register_1_q), .in1(register_2_q), .in2(register_3_q), .in3(register_4_q), .out(multiplexer_2_out),
    .sel(Reg_B));
  _5__ALU u_5_alu_1 (
    .Arguments(multiplexer_1_out), .in_2(Which_function), ._0__Addition(multiplexer_2_out), .Output(out_6));

  // Notes on the sheet:
  //   Which register to load
  //   What value to load
  //   Clock signal
  //   Loading registers and then doing math with their contents
  //   0: plus
  //   1: minus
  //   2: negate
  //   3: pass through
endmodule

module _8__CPB_B (
  input  [1:0] in_1,
  input  [1:0] Reg_A,
  input  [1:0] Reg_B,
  input  [1:0] Which_function,
  input  in_5,
  input  [7:0] in_6,
  output [7:0] Output
);

  wire button_1_out, decoder_1_out0, decoder_1_out1, decoder_1_out2, decoder_1_out3;
  wire [7:0] multiplexer_1_out, multiplexer_2_out, multiplexer_3_out, register_1_q, register_2_q,
       register_3_q, register_4_q;

  Decoder #(.select(2), .enable("false")) decoder_1 (
    .out0(decoder_1_out0), .out1(decoder_1_out1), .out2(decoder_1_out2), .out3(decoder_1_out3), .sel(in_1));
  Button button_1 (.out(button_1_out));
  Multiplexer #(.width(8), .enable("false")) multiplexer_1 (
    .in0(in_6), .in1(Output), .out(multiplexer_1_out));  // open: sel
  Register register_1 (.D(multiplexer_1_out), .en(decoder_1_out0), .Q(register_1_q), .clk(button_1_out));  // open: clr
  Register register_2 (.D(multiplexer_1_out), .en(decoder_1_out1), .Q(register_2_q), .clk(button_1_out));  // open: clr
  Register register_3 (.D(multiplexer_1_out), .en(decoder_1_out2), .Q(register_3_q), .clk(button_1_out));  // open: clr
  Register register_4 (.D(multiplexer_1_out), .en(decoder_1_out3), .Q(register_4_q), .clk(button_1_out));  // open: clr
  Multiplexer #(.select(2), .width(8), .enable("false")) multiplexer_2 (
    .in0(register_1_q), .in1(register_2_q), .in2(register_3_q), .in3(register_4_q), .out(multiplexer_2_out),
    .sel(Reg_A));
  Multiplexer #(.select(2), .width(8), .enable("false")) multiplexer_3 (
    .in0(register_1_q), .in1(register_2_q), .in2(register_3_q), .in3(register_4_q), .out(multiplexer_3_out),
    .sel(Reg_B));
  _5__ALU u_5_alu_1 (
    .Arguments(multiplexer_2_out), .in_2(Which_function), ._0__Addition(multiplexer_3_out), .Output(Output));

  // Notes on the sheet:
  //   Load from ALU or literal
  //   Which register to load
  //   Clock signal
  //   What value to load
  //   Putting the math results back into the registers
  //   0: Add
  //   1: Sub
  //   2: Negate
  //   3: Pass through
endmodule

module _9__RAM (
  output [3:0] Output,
  output [3:0] Address
);

  wire button_1_out;

  Button button_1 (.out(button_1_out));
  Counter #(.width(4), .max('hf)) counter_1 (
    .count(button_1_out), .Q(Address), .clk(button_1_out));  // open: load, D, carry, clr
  RAM #(.addrWidth(4), .dataWidth(4)) ram_1 (.addr(Address), .data(Output));  // open: sel, clk, ld, clr

  // Notes on the sheet:
  //   Clock
  //   Counter
  //   Memory is an array of numbered registers
  //   Memory
  //   It takes in a binary number and outputs that registers value 
endmodule

module _10__CPU_C (
  output [7:0] Output
);

  wire button_1_out, button_2_out, button_3_out, decoder_1_out0, decoder_1_out1, decoder_1_out2,
       decoder_1_out3;
  wire [7:0] counter_1_q, multiplexer_1_out, multiplexer_2_out, multiplexer_3_out, ram_1_data_2,
       register_1_q, register_2_q, register_3_q, register_4_q;
  wire [16:0] ram_1_data;

  Counter counter_1 (
    .count(button_2_out), .Q(counter_1_q), .clk(button_2_out), .clr(button_1_out));  // open: load, D, carry
  Button button_1 (.out(button_1_out));
  Decoder #(.select(2), .enable("false")) decoder_1 (
    .out0(decoder_1_out0), .out1(decoder_1_out1), .out2(decoder_1_out2), .out3(decoder_1_out3),
    .sel(ram_1_data[2:1]));
  Button button_2 (.out(button_2_out));
  Multiplexer #(.width(8), .enable("false")) multiplexer_1 (
    .in0(ram_1_data_2), .in1(Output), .out(multiplexer_1_out), .sel(ram_1_data[0]));
  RAM #(.dataWidth(17)) ram_1 (
    .addr(counter_1_q), .data({ram_1_data[16:11], ram_1_data_2, ram_1_data[2:0]}));  // open: sel, clk, ld, clr
  Register register_1 (
    .D(multiplexer_1_out), .en(decoder_1_out0), .Q(register_1_q), .clk(button_2_out), .clr(button_3_out));
  Register register_2 (
    .D(multiplexer_1_out), .en(decoder_1_out1), .Q(register_2_q), .clk(button_2_out), .clr(button_3_out));
  Register register_3 (
    .D(multiplexer_1_out), .en(decoder_1_out2), .Q(register_3_q), .clk(button_2_out), .clr(button_3_out));
  Register register_4 (
    .D(multiplexer_1_out), .en(decoder_1_out3), .Q(register_4_q), .clk(button_2_out), .clr(button_3_out));
  Button button_3 (.out(button_3_out));
  Multiplexer #(.select(2), .width(8), .enable("false")) multiplexer_2 (
    .in0(register_1_q), .in1(register_2_q), .in2(register_3_q), .in3(register_4_q), .out(multiplexer_2_out),
    .sel(ram_1_data[12:11]));
  Multiplexer #(.select(2), .width(8), .enable("false")) multiplexer_3 (
    .in0(register_1_q), .in1(register_2_q), .in2(register_3_q), .in3(register_4_q), .out(multiplexer_3_out),
    .sel(ram_1_data[14:13]));
  _5__ALU u_5_alu_1 (
    .Arguments(multiplexer_2_out), .in_2(ram_1_data[16:15]), ._0__Addition(multiplexer_3_out), .Output(Output));

  // Notes on the sheet:
  //   Which register to load
  //   Program
  //   Counter
  //   Reset
  //   Clock signal
  //   <---
  //   Reset
  //   Load from literal
  //   or ALU result
  //   <- What literal to load
  //   Instead of many input pins, lets use RAM
  //   Reg A
  //   Reg B
  //   Which function
  //   ALU result
endmodule

module _11__CPU_D (
  output [7:0] Output
);

  wire button_1_out, button_2_out, decoder_1_out0, decoder_1_out1, decoder_1_out2, decoder_1_out3,
       decoder_1_out4, decoder_1_out5, decoder_1_out6, decoder_1_out7, not_1_out;
  wire [7:0] counter_1_q, multiplexer_1_out, multiplexer_2_out, multiplexer_3_out, register_1_q,
       register_2_q, register_3_q, register_4_q, register_5_q, register_6_q, register_7_q;
  wire [19:0] ram_1_data;

  Decoder #(.select(3), .enable("false")) decoder_1 (
    .out0(decoder_1_out0), .out1(decoder_1_out1), .out2(decoder_1_out2), .out3(decoder_1_out3),
    .out4(decoder_1_out4), .out5(decoder_1_out5), .out6(decoder_1_out6), .out7(decoder_1_out7),
    .sel(ram_1_data[3:1]));
  not not_1 (not_1_out, decoder_1_out7);
  Button button_1 (.out(button_1_out));
  Multiplexer #(.width(8), .enable("false")) multiplexer_1 (
    .in0(ram_1_data[11:4]), .in1(Output), .out(multiplexer_1_out), .sel(ram_1_data[0]));
  RAM #(.dataWidth(20)) ram_1 (.addr(counter_1_q), .data(ram_1_data));  // open: sel, clk, ld, clr
  Register register_1 (
    .D(multiplexer_1_out), .en(decoder_1_out0), .Q(register_1_q), .clk(button_1_out), .clr(button_2_out));
  Register register_2 (
    .D(multiplexer_1_out), .en(decoder_1_out1), .Q(register_2_q), .clk(button_1_out), .clr(button_2_out));
  Register register_3 (
    .D(multiplexer_1_out), .en(decoder_1_out2), .Q(register_3_q), .clk(button_1_out), .clr(button_2_out));
  Register register_4 (
    .D(multiplexer_1_out), .en(decoder_1_out3), .Q(register_4_q), .clk(button_1_out), .clr(button_2_out));
  Register register_5 (
    .D(multiplexer_1_out), .en(decoder_1_out4), .Q(register_5_q), .clk(button_1_out), .clr(button_2_out));
  Register register_6 (
    .D(multiplexer_1_out), .en(decoder_1_out5), .Q(register_6_q), .clk(button_1_out), .clr(button_2_out));
  Register register_7 (
    .D(multiplexer_1_out), .en(decoder_1_out6), .Q(register_7_q), .clk(button_1_out), .clr(button_2_out));
  Counter counter_1 (
    .load(decoder_1_out7), .D(multiplexer_1_out), .count(not_1_out), .Q(counter_1_q), .clk(button_1_out),
    .clr(button_2_out));  // open: carry
  Button button_2 (.out(button_2_out));
  Multiplexer #(.select(3), .width(8), .enable("false")) multiplexer_2 (
    .in0(register_1_q), .in1(register_2_q), .in2(register_3_q), .in3(register_4_q), .in4(register_5_q),
    .in5(register_6_q), .in6(register_7_q), .in7(counter_1_q), .out(multiplexer_2_out),
    .sel(ram_1_data[14:12]));
  Multiplexer #(.select(3), .width(8), .enable("false")) multiplexer_3 (
    .in0(register_1_q), .in1(register_2_q), .in2(register_3_q), .in3(register_4_q), .in4(register_5_q),
    .in5(register_6_q), .in6(register_7_q), .in7(counter_1_q), .out(multiplexer_3_out),
    .sel(ram_1_data[17:15]));
  _5__ALU u_5_alu_1 (
    .Arguments(multiplexer_2_out), .in_2(ram_1_data[19:18]), ._0__Addition(multiplexer_3_out), .Output(Output));

  // Notes on the sheet:
  //   Clock signal
  //   0
  //   1
  //   2
  //   3
  //   4
  //   5
  //   6
  //   7
  //   Reset
  //   It's register 7
  //   2: reg1 -> reg0
  //   3: reg2 -> reg1
  //   Jump statements (non-conditional)
  //   Let's treat the Program Counter as a normal register.
  //   Fibonacci:
  //   0: Load 1 into reg 1
  //   1: reg0 + reg1 -> reg2
  //   4: go to instruction number 1
endmodule

module _12__ALU_2 (
  input  [7:0] in_1,
  input  [3:0] in_2,
  input  [7:0] _0__Plus,
  input  [7:0] in_4,
  input  [7:0] in_5,
  output [7:0] Output
);

  wire comparator_1_eq, comparator_1_gt, comparator_1_lt, comparator_2_eq, comparator_2_gt, comparator_2_lt,
       not_1_out, or_2_out;
  wire [7:0] adder_1_out, adder_2_out, and_1_out, bit_extender_1_out, bit_extender_2_out, bit_extender_3_out,
       bit_extender_4_out, multiplexer_1_out, multiplexer_2_out, multiplexer_3_out, negator_1_out, or_1_out,
       subtractor_1_out;

  Adder adder_1 (.a(in_1), .b(_0__Plus), .out(adder_1_out));  // open: cin, cout
  Subtractor subtractor_1 (.a(in_1), .b(_0__Plus), .out(subtractor_1_out));  // open: bin, bout
  Negator negator_1 (.in(in_1), .out(negator_1_out));
  assign and_1_out = in_1 & _0__Plus;  // AND_Gate and_1, 8 bits wide
  assign or_1_out = in_1 | _0__Plus;  // OR_Gate or_1, 8 bits wide
  Comparator comparator_1 (.a(in_1), .b(_0__Plus), .gt(comparator_1_gt), .eq(comparator_1_eq), .lt(comparator_1_lt));
  Comparator comparator_2 (.a(in_1), .b(_0__Plus), .gt(comparator_2_gt), .eq(comparator_2_eq), .lt(comparator_2_lt));
  or or_2 (or_2_out, in_1[0], in_1[1], in_1[2], in_1[3], in_1[4], in_1[5], in_1[6], in_1[7]);
  not not_1 (not_1_out, or_2_out);
  Multiplexer #(.width(8), .enable("false")) multiplexer_1 (
    .in0(adder_2_out), .in1(in_4), .out(multiplexer_1_out), .sel(comparator_2_gt));
  Multiplexer #(.width(8), .enable("false")) multiplexer_2 (
    .in0(adder_2_out), .in1(in_4), .out(multiplexer_2_out), .sel(comparator_2_eq));
  Multiplexer #(.width(8), .enable("false")) multiplexer_3 (
    .in0(adder_2_out), .in1(in_4), .out(multiplexer_3_out), .sel(comparator_2_lt));
  Adder adder_2 (.a(in_5), .b(8'h1), .out(adder_2_out));  // open: cin, cout
  assign bit_extender_1_out = {{7{1'b0}}, not_1_out};  // Bit_Extender bit_extender_1
  assign bit_extender_2_out = {{7{1'b0}}, comparator_1_gt};  // Bit_Extender bit_extender_2
  assign bit_extender_3_out = {{7{1'b0}}, comparator_1_eq};  // Bit_Extender bit_extender_3
  assign bit_extender_4_out = {{7{1'b0}}, comparator_1_lt};  // Bit_Extender bit_extender_4
  Multiplexer #(.select(4), .width(8), .enable("false")) multiplexer_4 (
    .in0(adder_1_out), .in1(subtractor_1_out), .in2(negator_1_out), .in3(in_1), .in4(and_1_out),
    .in5(or_1_out), .in6(bit_extender_1_out), .in7(bit_extender_2_out), .in8(bit_extender_3_out),
    .in9(bit_extender_4_out), .in10(multiplexer_1_out), .in11(multiplexer_2_out), .in12(multiplexer_3_out),
    .out(Output), .sel(in_2));  // open: in13, in14, in15

  // Notes on the sheet:
  //   Reg A
  //   Reg B
  //   3: Pass through
  //   6: Boolean Inverter
  //   0 = false
  //   !0 = true
  //   7: Greater than
  //   8: Equal
  //   9: Less than
  //   10: Jump if >
  //   11: Jump if =
  //   12: Jump if <
  //   1: Minus
  //   2: Negator
  //   4: And
  //   5: Or
  //   New PC value
  //   Old PC value
  //   Function Selector
  //   We increment because these instrutions
  //   override the PC's auto increment 
endmodule

module _13__CPU_E (
  output [7:0] Output
);

  wire button_1_out, button_2_out, decoder_1_out0, decoder_1_out1, decoder_1_out2, decoder_1_out3,
       decoder_1_out4, decoder_1_out5, decoder_1_out6, decoder_1_out7, not_1_out;
  wire [7:0] counter_1_q, multiplexer_1_out, multiplexer_2_out, multiplexer_3_out, multiplexer_4_out,
       register_1_q, register_2_q, register_3_q, register_4_q, register_5_q, register_6_q, register_7_q;
  wire [24:0] ram_1_data;

  Decoder #(.select(3), .enable("false")) decoder_1 (
    .out0(decoder_1_out0), .out1(decoder_1_out1), .out2(decoder_1_out2), .out3(decoder_1_out3),
    .out4(decoder_1_out4), .out5(decoder_1_out5), .out6(decoder_1_out6), .out7(decoder_1_out7),
    .sel(ram_1_data[3:1]));
  not not_1 (not_1_out, decoder_1_out7);
  Button button_1 (.out(button_1_out));
  Multiplexer #(.width(8), .enable("false")) multiplexer_1 (
    .in0(ram_1_data[11:4]), .in1(Output), .out(multiplexer_1_out), .sel(ram_1_data[0]));
  RAM #(.dataWidth(25)) ram_1 (.addr(counter_1_q), .data(ram_1_data));  // open: sel, clk, ld, clr
  Register register_1 (
    .D(multiplexer_1_out), .en(decoder_1_out0), .Q(register_1_q), .clk(button_1_out), .clr(button_2_out));
  Register register_2 (
    .D(multiplexer_1_out), .en(decoder_1_out1), .Q(register_2_q), .clk(button_1_out), .clr(button_2_out));
  Register register_3 (
    .D(multiplexer_1_out), .en(decoder_1_out2), .Q(register_3_q), .clk(button_1_out), .clr(button_2_out));
  Register register_4 (
    .D(multiplexer_1_out), .en(decoder_1_out3), .Q(register_4_q), .clk(button_1_out), .clr(button_2_out));
  Register register_5 (
    .D(multiplexer_1_out), .en(decoder_1_out4), .Q(register_5_q), .clk(button_1_out), .clr(button_2_out));
  Register register_6 (
    .D(multiplexer_1_out), .en(decoder_1_out5), .Q(register_6_q), .clk(button_1_out), .clr(button_2_out));
  Register register_7 (
    .D(multiplexer_1_out), .en(decoder_1_out6), .Q(register_7_q), .clk(button_1_out), .clr(button_2_out));
  Counter counter_1 (
    .load(decoder_1_out7), .D(multiplexer_1_out), .count(not_1_out), .Q(counter_1_q), .clk(button_1_out),
    .clr(button_2_out));  // open: carry
  Button button_2 (.out(button_2_out));
  Multiplexer #(.select(3), .width(8), .enable("false")) multiplexer_2 (
    .in0(register_1_q), .in1(register_2_q), .in2(register_3_q), .in3(register_4_q), .in4(register_5_q),
    .in5(register_6_q), .in6(register_7_q), .in7(counter_1_q), .out(multiplexer_2_out),
    .sel(ram_1_data[14:12]));
  Multiplexer #(.select(3), .width(8), .enable("false")) multiplexer_3 (
    .in0(register_1_q), .in1(register_2_q), .in2(register_3_q), .in3(register_4_q), .in4(register_5_q),
    .in5(register_6_q), .in6(register_7_q), .in7(counter_1_q), .out(multiplexer_3_out),
    .sel(ram_1_data[17:15]));
  Multiplexer #(.select(3), .width(8), .enable("false")) multiplexer_4 (
    .in0(register_1_q), .in1(register_2_q), .in2(register_3_q), .in3(register_4_q), .in4(register_5_q),
    .in5(register_6_q), .in6(register_7_q), .in7(counter_1_q), .out(multiplexer_4_out),
    .sel(ram_1_data[20:18]));
  _12__ALU_2 u_12_alu_2_1 (
    .in_1(multiplexer_2_out), .in_2(ram_1_data[24:21]), ._0__Plus(multiplexer_3_out),
    .in_4(multiplexer_4_out), .Output(Output), .in_5(counter_1_q));

  // Notes on the sheet:
  //   Let's use our new ALU
  //   and boolean evaluations
  //   This lets us do conditional jumps
  //   Clock signal
  //   Reset
endmodule

module _14__CPU_F (
  output [7:0] Output
);

  wire and_1_out, button_1_out, button_2_out, button_3_out, decoder_1_out0, decoder_1_out1, decoder_1_out2,
       decoder_1_out3, decoder_1_out4, decoder_1_out5, decoder_1_out6, decoder_1_out7, not_1_out;
  wire [1:0] ram_1_data;
  wire [6:0] keyboard_1_data;
  wire [7:0] bit_extender_1_out, counter_1_q, multiplexer_1_out, multiplexer_2_out, multiplexer_3_out,
       multiplexer_4_out, register_1_q, register_2_q, register_3_q, register_4_q, register_5_q, register_6_q,
       register_7_q;
  wire [25:2] ram_1_data_2;

  Decoder #(.select(3), .enable("false")) decoder_1 (
    .out0(decoder_1_out0), .out1(decoder_1_out1), .out2(decoder_1_out2), .out3(decoder_1_out3),
    .out4(decoder_1_out4), .out5(decoder_1_out5), .out6(decoder_1_out6), .out7(decoder_1_out7),
    .sel(ram_1_data_2[4:2]));
  Keyboard keyboard_1 (.clk(button_2_out), .re(and_1_out), .clr(button_1_out), .data(keyboard_1_data));  // open: avail
  and and_1 (and_1_out, ram_1_data[0], ram_1_data[1]);
  Button button_1 (.out(button_1_out));
  not not_1 (not_1_out, decoder_1_out7);
  Button button_2 (.out(button_2_out));
  Multiplexer #(.select(2), .width(8), .enable("false")) multiplexer_1 (
    .in0(ram_1_data_2[12:5]), .in1(Output), .in3(bit_extender_1_out), .out(multiplexer_1_out),
    .sel(ram_1_data));  // open: in2
  RAM #(.dataWidth(26)) ram_1 (.addr(counter_1_q), .data({ram_1_data_2, ram_1_data}));  // open: sel, clk, ld, clr
  Register register_1 (
    .D(multiplexer_1_out), .en(decoder_1_out0), .Q(register_1_q), .clk(button_2_out), .clr(button_3_out));
  Register register_2 (
    .D(multiplexer_1_out), .en(decoder_1_out1), .Q(register_2_q), .clk(button_2_out), .clr(button_3_out));
  Register register_3 (
    .D(multiplexer_1_out), .en(decoder_1_out2), .Q(register_3_q), .clk(button_2_out), .clr(button_3_out));
  Register register_4 (
    .D(multiplexer_1_out), .en(decoder_1_out3), .Q(register_4_q), .clk(button_2_out), .clr(button_3_out));
  Register register_5 (
    .D(multiplexer_1_out), .en(decoder_1_out4), .Q(register_5_q), .clk(button_2_out), .clr(button_3_out));
  Register register_6 (
    .D(multiplexer_1_out), .en(decoder_1_out5), .Q(register_6_q), .clk(button_2_out), .clr(button_3_out));
  Register register_7 (
    .D(multiplexer_1_out), .en(decoder_1_out6), .Q(register_7_q), .clk(button_2_out), .clr(button_3_out));
  Counter counter_1 (
    .load(decoder_1_out7), .D(multiplexer_1_out), .count(not_1_out), .Q(counter_1_q), .clk(button_2_out),
    .clr(button_3_out));  // open: carry
  Button button_3 (.out(button_3_out));
  assign bit_extender_1_out = {{1{1'b0}}, keyboard_1_data};  // Bit_Extender bit_extender_1
  Multiplexer #(.select(3), .width(8), .enable("false")) multiplexer_2 (
    .in0(register_1_q), .in1(register_2_q), .in2(register_3_q), .in3(register_4_q), .in4(register_5_q),
    .in5(register_6_q), .in6(register_7_q), .in7(counter_1_q), .out(multiplexer_2_out),
    .sel(ram_1_data_2[15:13]));
  Multiplexer #(.select(3), .width(8), .enable("false")) multiplexer_3 (
    .in0(register_1_q), .in1(register_2_q), .in2(register_3_q), .in3(register_4_q), .in4(register_5_q),
    .in5(register_6_q), .in6(register_7_q), .in7(counter_1_q), .out(multiplexer_3_out),
    .sel(ram_1_data_2[18:16]));
  Multiplexer #(.select(3), .width(8), .enable("false")) multiplexer_4 (
    .in0(register_1_q), .in1(register_2_q), .in2(register_3_q), .in3(register_4_q), .in4(register_5_q),
    .in5(register_6_q), .in6(register_7_q), .in7(counter_1_q), .out(multiplexer_4_out),
    .sel(ram_1_data_2[21:19]));
  _12__ALU_2 u_12_alu_2_1 (
    .in_1(multiplexer_2_out), .in_2(ram_1_data_2[25:22]), ._0__Plus(multiplexer_3_out),
    .in_4(multiplexer_4_out), .Output(Output), .in_5(counter_1_q));

  // Notes on the sheet:
  //   Let's add keyboard input
  //   Keyboard Buffer
  //   Clear buffer
  //   Clock signal
  //   Reset
endmodule

module _15__CPU_G (
  output [7:0] Output
);

  wire and_1_out, button_1_out, button_2_out, button_3_out, decoder_1_out0, decoder_1_out1, decoder_1_out2,
       decoder_1_out3, decoder_1_out4, decoder_1_out5, decoder_1_out6, decoder_1_out7, not_1_out;
  wire [1:0] ram_1_data;
  wire [6:0] keyboard_1_data;
  wire [7:0] bit_extender_1_out, counter_1_q, multiplexer_1_out, multiplexer_2_out, multiplexer_3_out,
       multiplexer_4_out, register_1_q, register_2_q, register_3_q, register_4_q, register_5_q, register_6_q;
  wire [25:2] ram_1_data_2;

  Decoder #(.select(3), .enable("false")) decoder_1 (
    .out0(decoder_1_out0), .out1(decoder_1_out1), .out2(decoder_1_out2), .out3(decoder_1_out3),
    .out4(decoder_1_out4), .out5(decoder_1_out5), .out6(decoder_1_out6), .out7(decoder_1_out7),
    .sel(ram_1_data_2[4:2]));
  Keyboard keyboard_1 (.clk(button_2_out), .re(and_1_out), .clr(button_1_out), .data(keyboard_1_data));  // open: avail
  and and_1 (and_1_out, ram_1_data[0], ram_1_data[1]);
  Button button_1 (.out(button_1_out));
  not not_1 (not_1_out, decoder_1_out7);
  Button button_2 (.out(button_2_out));
  Multiplexer #(.select(2), .width(8), .enable("false")) multiplexer_1 (
    .in1(Output), .in3(bit_extender_1_out), .out(multiplexer_1_out), .sel(ram_1_data));  // open: in0, in2
  RAM #(.dataWidth(26)) ram_1 (.addr(counter_1_q), .data({ram_1_data_2, ram_1_data}));  // open: sel, clk, ld, clr
  Register register_1 (
    .D(multiplexer_1_out), .en(decoder_1_out0), .Q(register_1_q), .clk(button_2_out), .clr(button_3_out));
  Register register_2 (
    .D(multiplexer_1_out), .en(decoder_1_out1), .Q(register_2_q), .clk(button_2_out), .clr(button_3_out));
  Register register_3 (
    .D(multiplexer_1_out), .en(decoder_1_out2), .Q(register_3_q), .clk(button_2_out), .clr(button_3_out));
  Register register_4 (
    .D(multiplexer_1_out), .en(decoder_1_out3), .Q(register_4_q), .clk(button_2_out), .clr(button_3_out));
  Register register_5 (
    .D(multiplexer_1_out), .en(decoder_1_out4), .Q(register_5_q), .clk(button_2_out), .clr(button_3_out));
  Register register_6 (
    .D(multiplexer_1_out), .en(decoder_1_out5), .Q(register_6_q), .clk(button_2_out), .clr(button_3_out));
  Counter counter_1 (
    .load(decoder_1_out7), .D(multiplexer_1_out), .count(not_1_out), .Q(counter_1_q), .clk(button_2_out),
    .clr(button_3_out));  // open: carry
  Button button_3 (.out(button_3_out));
  assign bit_extender_1_out = {{1{1'b0}}, keyboard_1_data};  // Bit_Extender bit_extender_1
  Multiplexer #(.select(3), .width(8), .enable("false")) multiplexer_2 (
    .in0(register_1_q), .in1(register_2_q), .in2(register_3_q), .in3(register_4_q), .in4(register_5_q),
    .in5(register_6_q), .in6(ram_1_data_2[12:5]), .in7(counter_1_q), .out(multiplexer_2_out),
    .sel(ram_1_data_2[15:13]));
  Multiplexer #(.select(3), .width(8), .enable("false")) multiplexer_3 (
    .in0(register_1_q), .in1(register_2_q), .in2(register_3_q), .in3(register_4_q), .in4(register_5_q),
    .in5(register_6_q), .in6(ram_1_data_2[12:5]), .in7(counter_1_q), .out(multiplexer_3_out),
    .sel(ram_1_data_2[18:16]));
  Multiplexer #(.select(3), .width(8), .enable("false")) multiplexer_4 (
    .in0(register_1_q), .in1(register_2_q), .in2(register_3_q), .in3(register_4_q), .in4(register_5_q),
    .in5(register_6_q), .in6(ram_1_data_2[12:5]), .in7(counter_1_q), .out(multiplexer_4_out),
    .sel(ram_1_data_2[21:19]));
  _12__ALU_2 u_12_alu_2_1 (
    .in_1(multiplexer_2_out), .in_2(ram_1_data_2[25:22]), ._0__Plus(multiplexer_3_out),
    .in_4(multiplexer_4_out), .Output(Output), .in_5(counter_1_q));
  TTY tty_1 (.data(multiplexer_1_out[6:0]), .clk(button_2_out), .we(decoder_1_out6), .clr(button_3_out));

  // Notes on the sheet:
  //   Lets add screen output
  //   and treat the literal as a reg
  //   Keyboard Buffer
  //   Clear Buffer
  //   Clock signal
  //   Reset
endmodule
