// Logisim project Lesson3.circ as structural Verilog
module zAluA (
  input  [7:0] Arguments,
  input  [1:0] in_2,
  input  [7:0] in_3,
  output [7:0] Output
);

  wire [7:0] adder_1_out, negator_1_out, subtractor_1_out;

  Adder adder_1 (.a(Arguments), .b(in_3), .out(adder_1_out));  // open: cin, cout
  Subtractor subtractor_1 (.a(Arguments), .b(in_3), .out(subtractor_1_out));  // open: bin, bout
  Negator negator_1 (.in(Arguments), .out(negator_1_out));
  Multiplexer #(.select(2), .width(8), .enable("false")) multiplexer_1 (
    .in0(adder_1_out), .in1(subtractor_1_out), .in2(negator_1_out), .in3(Arguments), .out(Output), .sel(in_2));

  // Notes on the sheet:
  //   0: Addition
  //   1: Subtraction
  //   2: Negation
  //   3: Pass through
  //   Function selector
endmodule
